# Fritzing sketch LED (saved by Fritzing 0.9.3b)
breadboards: 1

parts:
  R1 = Resistor [tolerance=±5% resistance=1k package=THT]
  R2 = Resistor [tolerance=±5% resistance=1k package=THT]
  LED1 = smd LED [color="Blue (470nm)" package="1206 [SMD]"]
  LED2 = smd LED [color="Orange (620nm)" package="1206 [SMD]"]
  Raspberry_Pi1 = Raspberry Pi B+

nets:
  N1: R1.Pin_0, LED1.cathode
  N2: R1.Pin_1, R2.Pin_1, Raspberry_Pi1.GND
  N3: R2.Pin_0, LED2.cathode
  N4: LED1.anode, Raspberry_Pi1.GPIO17
  N5: LED2.anode, Raspberry_Pi1.GPIO27
